# Fritzing sketch accledchange (saved by Fritzing 0.9.2b)
breadboards: 1

parts:
  Componente2 = Triple Axis Accelerometer Breakout - ADXL335
  Componente3 = Arduino Uno (Rev3)
  LED1 = LED - 5mm [color="Red (633nm)" package="5 mm [THT]"]
  R1 = Resistor [tolerance=±5% resistance=220 package=THT]
  LED2 = LED - 5mm [color="Yellow (585nm)" package="5 mm [THT]"]
  LED3 = LED - 5mm [color="Green (555nm)" package="5 mm [THT]"]
  R2 = Resistor [tolerance=±5% resistance=220 package=THT]
  R3 = Resistor [tolerance=±5% resistance=220 package=THT]

nets:
  N1: Componente2.ZOUT, Componente3.A0
  N2: Componente2.YOUT, Componente3.A1
  N3: Componente2.XOUT, Componente3.A2
  GND: Componente2.GND, Componente3.GND, LED1.cathode, LED2.cathode, LED3.cathode
  VCC: Componente2.VCC, Componente3.5V
  N4: Componente3.D9_PWM, R3.Pin_1
  N5: Componente3.D10_PWM/SS, R2.Pin_1
  N6: Componente3.D11_PWM/MOSI, R1.Pin_1
  N7: LED1.anode, R1.Pin_0
  N8: LED2.anode, R2.Pin_0
  N9: LED3.anode, R3.Pin_0
