# Fritzing sketch fled (saved by Fritzing 0.7.11b)
breadboards: 1

parts:
  LED1 = LED - 5mm [color="Red (633nm)" package="5 mm [THT]"]
  R1 = Resistor [tolerance=±5% resistance=220 package=THT]
  Componente1 = Arduino Uno (Rev3)
  S1 = Pushbutton [package="[THT]"]
  R2 = Resistor [tolerance=±5% resistance=220 package=THT]

nets:
  N1: LED1.cathode, Componente1.GND, R2.Pin_1
  N2: LED1.anode, R1.Pin_0
  N3: R1.Pin_1, Componente1.D13/SCK
  N4: Componente1.D10_PWM/SS, S1.Pin_1, S1.Pin_2, R2.Pin_0
  N5: Componente1.5V, S1.Pin_3, S1.Pin_4
